// Logisim project 3 to 8 decoder (primary gates).circ as structural Verilog
module _3_to_8_decoder (
  input  A,
  input  B,
  input  C,
  output d0,
  output d1,
  output d2,
  output d3,
  output d4,
  output d5,
  output d6,
  output d7
);

  wire not_1_out, not_2_out, not_3_out, not_4_out, not_5_out, not_6_out, not_7_out, not_8_out, not_9_out,
       not_10_out, not_11_out, not_12_out;

  not not_1 (not_1_out, A);
  not not_2 (not_2_out, B);
  not not_3 (not_3_out, C);
  not not_4 (not_4_out, A);
  not not_5 (not_5_out, B);
  not not_6 (not_6_out, A);
  not not_7 (not_7_out, C);
  not not_8 (not_8_out, A);
  not not_9 (not_9_out, B);
  not not_10 (not_10_out, C);
  not not_11 (not_11_out, B);
  not not_12 (not_12_out, C);
  and and_1 (d0, not_1_out, not_2_out, not_3_out);
  and and_2 (d1, not_4_out, not_5_out, C);
  and and_3 (d2, not_6_out, B, not_7_out);
  and and_4 (d3, not_8_out, B, C);
  and and_5 (d4, A, not_9_out, not_10_out);
  and and_6 (d5, A, not_11_out, C);
  and and_7 (d6, A, B, not_12_out);
  and and_8 (d7, A, B, C);
endmodule
