// Logisim project 3 to 8 decoder (using decoder).circ as structural Verilog: 1 circuit, main circuit main
module main (
  input  D2,
  input  D1,
  input  D0,
  output _0,
  output _1,
  output _2,
  output _3,
  output _4,
  output _5,
  output _6,
  output _7
);

  Decoder #(.select(3)) decoder_1 (
    .out0(_0), .out1(_1), .out2(_2), .out3(_3), .out4(_4), .out5(_5), .out6(_6), .out7(_7), .sel({D2, D1, D0}));  // open: en
endmodule
