// Logisim project 4 bit asynchronus counter.circ as structural Verilog: 1 circuit, main circuit main
module main (
  input  in_1,
  output out_2,
  output out_3,
  output out_4,
  output out_5
);

  wire A_qn, B_qn, C_qn, clock_1_out;

  Clock clock_1 (.out(clock_1_out));
  J_K_Flip_Flop A (.J(in_1), .clk(clock_1_out), .K(in_1), .Q(out_5), .Qn(A_qn));  // open: preset, en, reset
  J_K_Flip_Flop B (.J(in_1), .clk(A_qn), .K(in_1), .Q(out_4), .Qn(B_qn));  // open: preset, en, reset
  J_K_Flip_Flop C (.J(in_1), .clk(B_qn), .K(in_1), .Q(out_3), .Qn(C_qn));  // open: preset, en, reset
  J_K_Flip_Flop D (.J(in_1), .clk(C_qn), .K(in_1), .Q(out_2));  // open: Qn, preset, en, reset
  Hex_Digit_Display hex_digit_display_1 (.value({out_2, out_3, out_4, out_5}));  // open: dp
endmodule
