// Logisim project 4-8 decoder using 2-4 decoders only.circ as structural Verilog: 1 circuit, main circuit main
module main (
  input  [1:0] in_1,
  input  [1:0] in_2,
  input  in_3,
  output out_4,
  output out_5,
  output out_6,
  output out_7,
  output out_8,
  output out_9,
  output out_10,
  output out_11,
  output out_12,
  output out_13,
  output out_14,
  output out_15,
  output out_16,
  output out_17,
  output out_18,
  output out_19
);

  wire decoder_1_out0, decoder_1_out1, decoder_1_out2, decoder_1_out3, undriven;

  Decoder #(.select(2)) decoder_1 (
    .out0(decoder_1_out0), .out1(decoder_1_out1), .out2(decoder_1_out2), .out3(decoder_1_out3), .sel(in_2),
    .en(undriven));
  Decoder #(.select(2)) decoder_2 (
    .out0(out_4), .out1(out_5), .out2(out_6), .out3(out_7), .sel(in_1), .en(decoder_1_out0));
  Decoder #(.select(2)) decoder_3 (
    .out0(out_8), .out1(out_9), .out2(out_10), .out3(out_11), .sel(in_1), .en(decoder_1_out1));
  Decoder #(.select(2)) decoder_4 (
    .out0(out_12), .out1(out_13), .out2(out_14), .out3(out_15), .sel(in_1), .en(decoder_1_out2));
  Decoder #(.select(2)) decoder_5 (
    .out0(out_16), .out1(out_17), .out2(out_18), .out3(out_19), .sel(in_1), .en(decoder_1_out3));
endmodule
