// Logisim project 8 to 3 Encoder (using priority encoder).circ as structural Verilog: 1 circuit, main circuit main
module main (
  input  Y0,
  input  Y1,
  input  Y2,
  input  Y3,
  input  Y4,
  input  Y5,
  input  Y6,
  input  Y7,
  input  in_9,
  output A2,
  output A1,
  output A0
);

  wire undriven;

  Priority_Encoder priority_encoder_1 (
    .in0(Y0), .in1(Y1), .in2(Y2), .in3(Y3), .in4(Y4), .in5(Y5), .in6(Y6), .in7(Y7), .out({A2, A1, A0}),
    .en_in(undriven));  // open: gs, en_out
endmodule
