// Logisim project BCD to greycode.circ as structural Verilog
module bcd_to_grey (
  input  W,
  input  X,
  input  Y,
  input  Z,
  output G3,
  output G2,
  output G1,
  output G0
);

  or or_1 (G2, W, X);
  xor xor_1 (G1, X, Y);
  xor xor_2 (G0, Y, Z);

  assign G3 = W;
endmodule
